// Logisim project 8_bit_CPU.circ as structural Verilog: 3 circuits, main circuit main
module main (
);

  wire [7:0] undriven;

  ROM #(.dataWidth(24)) rom_1 (.addr(undriven));  // open: data
  RAM ram_1 ();  // open: addr, we, oe, clk, din, dout
endmodule

module D_type_flip_flop (
  input  DATA,
  input  CLK,
  output Q,
  output NOT_Q
);

  wire nand_1_out, nand_2_out, not_1_out;

  not not_1 (not_1_out, DATA);
  nand nand_1 (nand_1_out, DATA, CLK);
  nand nand_2 (nand_2_out, not_1_out, CLK);
  nand nand_3 (Q, nand_1_out, NOT_Q);
  nand nand_4 (NOT_Q, Q, nand_2_out);
endmodule

module register_8bit (
  input  [7:0] DATA,
  input  WRITE,
  output [7:0] Q,
  output [7:0] NOT_Q
);

  D_type_flip_flop d_type_flip_flop_1 (.DATA(DATA[0]), .CLK(WRITE), .Q(Q[0]), .NOT_Q(NOT_Q[0]));
  D_type_flip_flop d_type_flip_flop_2 (.DATA(DATA[1]), .CLK(WRITE), .Q(Q[1]), .NOT_Q(NOT_Q[1]));
  D_type_flip_flop d_type_flip_flop_3 (.DATA(DATA[2]), .CLK(WRITE), .Q(Q[2]), .NOT_Q(NOT_Q[2]));
  D_type_flip_flop d_type_flip_flop_4 (.DATA(DATA[3]), .CLK(WRITE), .Q(Q[3]), .NOT_Q(NOT_Q[3]));
  D_type_flip_flop d_type_flip_flop_5 (.DATA(DATA[4]), .CLK(WRITE), .Q(Q[4]), .NOT_Q(NOT_Q[4]));
  D_type_flip_flop d_type_flip_flop_6 (.DATA(DATA[5]), .CLK(WRITE), .Q(Q[5]), .NOT_Q(NOT_Q[5]));
  D_type_flip_flop d_type_flip_flop_7 (.DATA(DATA[6]), .CLK(WRITE), .Q(Q[6]), .NOT_Q(NOT_Q[6]));
  D_type_flip_flop d_type_flip_flop_8 (.DATA(DATA[7]), .CLK(WRITE), .Q(Q[7]), .NOT_Q(NOT_Q[7]));
endmodule
